// Logisim project StateEq.circ as structural Verilog: 4 circuits, main circuit main
module main (
  input  STP,
  input  SM_plus_minus,
  input  SBT,
  output M0,
  output M1,
  output A,
  output B,
  output C
);

  wire clock_1_out, lift2_1_a2, lift2_1_b2, lift2_1_c2, or_1_out, or_2_out, or_3_out, PB1_out, PB2_out,
       PB3_out, RESET_out, SBT_out, SM_plus_minus_out, STP_out;

  Button u_STP (.out(STP_out));
  or or_1 (or_1_out, STP_out, STP);
  Button u_SM_plus_minus (.out(SM_plus_minus_out));
  or or_2 (or_2_out, SM_plus_minus_out, SM_plus_minus);
  Button u_SBT (.out(SBT_out));
  or or_3 (or_3_out, SBT_out, SBT);
  Button RESET (.out(RESET_out));
  Clock clock_1 (.out(clock_1_out));
  Button PB3 (.out(PB3_out));
  Button PB2 (.out(PB2_out));
  Button PB1 (.out(PB1_out));
  Lift2 lift2_1 (
    .A(A), .B(B), .C(C), .PB1(PB1_out), .PB2(PB2_out), .PB3(PB3_out), .STP(or_1_out), .SMP(or_2_out),
    .SMM(or_2_out), .SBT(or_3_out), .A2(lift2_1_a2), .B2(lift2_1_b2), .C2(lift2_1_c2), .M0(M0), .M1(M1));
  D_Flip_Flop d_ff_1 (.clk(clock_1_out), .D(lift2_1_a2), .Q(A), .preset(RESET_out));  // open: Qn, en, reset
  D_Flip_Flop d_ff_2 (.clk(clock_1_out), .D(lift2_1_b2), .Q(B), .preset(RESET_out));  // open: Qn, en, reset
  D_Flip_Flop d_ff_3 (.clk(clock_1_out), .D(lift2_1_c2), .Q(C), .reset(RESET_out));  // open: Qn, preset, en
endmodule

module Lift1 (
  input  A,
  input  B,
  input  C,
  input  PB1,
  input  PB2,
  input  PB3,
  input  STP,
  input  SMP,
  input  SMM,
  input  SBT,
  output A2,
  output B2,
  output C2,
  output M0,
  output M1
);

  wire and_1_out, and_2_out, and_3_out, and_4_out, and_5_out, and_6_out, and_7_out, and_8_out, and_9_out,
       and_10_out, and_11_out, and_12_out, and_13_out, and_14_out, and_15_out, and_16_out, and_17_out,
       and_18_out, and_19_out, and_20_out, and_21_out, and_22_out, and_23_out, and_24_out, and_25_out,
       and_26_out, and_27_out, and_28_out, and_29_out, and_30_out, and_31_out, and_32_out, and_33_out,
       and_34_out, and_35_out, and_36_out, and_37_out, and_38_out, and_39_out, and_40_out, and_41_out,
       and_42_out, and_43_out, and_44_out, and_45_out, and_46_out, and_47_out, and_48_out, and_49_out,
       and_50_out, and_51_out, and_52_out, and_53_out, and_54_out, and_55_out, and_56_out, and_57_out,
       and_58_out, and_59_out, and_60_out, and_61_out, and_62_out, and_63_out, and_64_out, and_65_out,
       and_66_out, and_67_out, and_68_out, and_69_out, and_70_out, and_71_out, and_72_out, and_73_out,
       and_74_out, and_75_out, and_76_out, and_77_out, and_78_out, and_79_out, and_80_out, and_81_out,
       and_82_out, and_83_out, and_84_out, and_85_out, and_86_out, and_87_out, and_88_out, and_89_out,
       and_90_out, not_1_out, not_2_out, not_3_out, not_4_out, not_5_out, not_6_out, not_7_out, not_8_out,
       not_9_out, not_10_out, not_11_out, not_12_out, not_13_out, not_14_out, not_15_out, not_16_out,
       not_17_out, not_18_out, not_19_out, not_20_out, not_21_out, not_22_out, not_23_out, not_24_out,
       not_25_out, not_26_out, not_27_out, not_28_out, not_29_out, not_30_out, not_31_out, not_32_out,
       not_33_out, not_34_out, not_35_out, not_36_out, not_37_out, not_38_out, not_39_out, not_40_out,
       not_41_out, not_42_out, not_43_out, not_44_out, not_45_out, not_46_out, not_47_out, not_48_out,
       not_49_out, not_50_out, not_51_out, not_52_out, not_53_out, not_54_out, not_55_out, not_56_out,
       not_57_out, not_58_out, not_59_out, not_60_out, not_61_out, not_62_out, not_63_out, not_64_out,
       not_65_out, not_66_out, not_67_out, not_68_out, not_69_out, not_70_out, not_71_out, not_72_out,
       not_73_out, not_74_out, not_75_out, not_76_out, not_77_out, not_78_out, not_79_out, not_80_out,
       not_81_out, not_82_out, not_83_out, not_84_out, not_85_out, not_86_out, not_87_out, not_88_out,
       not_89_out, not_90_out, not_91_out, not_92_out, not_93_out, not_94_out, not_95_out, not_96_out,
       not_97_out, not_98_out, not_99_out, not_100_out, not_101_out, not_102_out, not_103_out, not_104_out,
       not_105_out, not_106_out, not_107_out, not_108_out, not_109_out, not_110_out, not_111_out,
       not_112_out, not_113_out, not_114_out, not_115_out, not_116_out, not_117_out, not_118_out,
       not_119_out, not_120_out, not_121_out, not_122_out, not_123_out, not_124_out, not_125_out,
       not_126_out, not_127_out, not_128_out, not_129_out, not_130_out, not_131_out, not_132_out,
       not_133_out, not_134_out, not_135_out, not_136_out, not_137_out, not_138_out, not_139_out,
       not_140_out, not_141_out, not_142_out, not_143_out, not_144_out, not_145_out, not_146_out,
       not_147_out, not_148_out, not_149_out, not_150_out, not_151_out, not_152_out, not_153_out,
       not_154_out, not_155_out, not_156_out, not_157_out, not_158_out, not_159_out, not_160_out,
       not_161_out, not_162_out, not_163_out, not_164_out, not_165_out, not_166_out, not_167_out,
       not_168_out, not_169_out, not_170_out, not_171_out, not_172_out, not_173_out, not_174_out,
       not_175_out, not_176_out, not_177_out, not_178_out, not_179_out, not_180_out, not_181_out,
       not_182_out, not_183_out, not_184_out, not_185_out, not_186_out, not_187_out, not_188_out,
       not_189_out, not_190_out, not_191_out, not_192_out, not_193_out, not_194_out, not_195_out,
       not_196_out, not_197_out, not_198_out, not_199_out, not_200_out, not_201_out, not_202_out,
       not_203_out, not_204_out, not_205_out, not_206_out, not_207_out, not_208_out, not_209_out,
       not_210_out, not_211_out, not_212_out, not_213_out, not_214_out, not_215_out, not_216_out,
       not_217_out, not_218_out, not_219_out, not_220_out, not_221_out, not_222_out, not_223_out,
       not_224_out, not_225_out, not_226_out, not_227_out, not_228_out, not_229_out, not_230_out,
       not_231_out, not_232_out, not_233_out, not_234_out, not_235_out, not_236_out, not_237_out,
       not_238_out, not_239_out, not_240_out, not_241_out, not_242_out, not_243_out, not_244_out,
       not_245_out, not_246_out, not_247_out, not_248_out, not_249_out, not_250_out, not_251_out,
       not_252_out, not_253_out, not_254_out, not_255_out, not_256_out, not_257_out;

  not not_1 (not_1_out, A);
  not not_2 (not_2_out, B);
  not not_3 (not_3_out, PB1);
  not not_4 (not_4_out, PB2);
  not not_5 (not_5_out, STP);
  not not_6 (not_6_out, B);
  not not_7 (not_7_out, PB1);
  not not_8 (not_8_out, PB2);
  not not_9 (not_9_out, A);
  not not_10 (not_10_out, B);
  not not_11 (not_11_out, PB1);
  not not_12 (not_12_out, PB2);
  not not_13 (not_13_out, B);
  not not_14 (not_14_out, PB1);
  not not_15 (not_15_out, PB2);
  not not_16 (not_16_out, SMM);
  not not_17 (not_17_out, A);
  not not_18 (not_18_out, B);
  not not_19 (not_19_out, PB2);
  not not_20 (not_20_out, PB3);
  not not_21 (not_21_out, SBT);
  not not_22 (not_22_out, B);
  not not_23 (not_23_out, PB2);
  not not_24 (not_24_out, PB3);
  not not_25 (not_25_out, SMP);
  not not_26 (not_26_out, B);
  not not_27 (not_27_out, PB2);
  not not_28 (not_28_out, PB3);
  not not_29 (not_29_out, B);
  not not_30 (not_30_out, PB2);
  not not_31 (not_31_out, PB3);
  not not_32 (not_32_out, A);
  not not_33 (not_33_out, C);
  not not_34 (not_34_out, PB1);
  not not_35 (not_35_out, PB3);
  not not_36 (not_36_out, SMP);
  not not_37 (not_37_out, A);
  not not_38 (not_38_out, C);
  not not_39 (not_39_out, PB1);
  not not_40 (not_40_out, PB3);
  not not_41 (not_41_out, SMM);
  not not_42 (not_42_out, A);
  not not_43 (not_43_out, C);
  not not_44 (not_44_out, PB1);
  not not_45 (not_45_out, PB3);
  not not_46 (not_46_out, C);
  not not_47 (not_47_out, PB1);
  not not_48 (not_48_out, PB3);
  not not_49 (not_49_out, A);
  not not_50 (not_50_out, C);
  not not_51 (not_51_out, PB2);
  not not_52 (not_52_out, PB3);
  not not_53 (not_53_out, B);
  not not_54 (not_54_out, STP);
  not not_55 (not_55_out, SMM);
  not not_56 (not_56_out, B);
  not not_57 (not_57_out, PB1);
  not not_58 (not_58_out, C);
  not not_59 (not_59_out, C);
  not not_60 (not_60_out, C);
  not not_61 (not_61_out, B);
  not not_62 (not_62_out, B);
  not not_63 (not_63_out, B);
  not not_64 (not_64_out, SMP);
  not not_65 (not_65_out, C);
  not not_66 (not_66_out, SBT);
  not not_67 (not_67_out, A);
  not not_68 (not_68_out, PB1);
  not not_69 (not_69_out, PB2);
  not not_70 (not_70_out, SMP);
  not not_71 (not_71_out, SMM);
  not not_72 (not_72_out, SBT);
  not not_73 (not_73_out, A);
  not not_74 (not_74_out, B);
  not not_75 (not_75_out, C);
  not not_76 (not_76_out, PB1);
  not not_77 (not_77_out, PB3);
  not not_78 (not_78_out, SMP);
  not not_79 (not_79_out, A);
  not not_80 (not_80_out, B);
  not not_81 (not_81_out, C);
  not not_82 (not_82_out, PB1);
  not not_83 (not_83_out, PB3);
  not not_84 (not_84_out, SMM);
  not not_85 (not_85_out, A);
  not not_86 (not_86_out, B);
  not not_87 (not_87_out, C);
  not not_88 (not_88_out, PB1);
  not not_89 (not_89_out, PB3);
  not not_90 (not_90_out, A);
  not not_91 (not_91_out, B);
  not not_92 (not_92_out, C);
  not not_93 (not_93_out, PB1);
  not not_94 (not_94_out, PB3);
  not not_95 (not_95_out, A);
  not not_96 (not_96_out, B);
  not not_97 (not_97_out, PB2);
  not not_98 (not_98_out, PB3);
  not not_99 (not_99_out, SBT);
  not not_100 (not_100_out, A);
  not not_101 (not_101_out, B);
  not not_102 (not_102_out, PB2);
  not not_103 (not_103_out, PB3);
  not not_104 (not_104_out, A);
  not not_105 (not_105_out, PB2);
  not not_106 (not_106_out, PB3);
  not not_107 (not_107_out, SMM);
  not not_108 (not_108_out, A);
  not not_109 (not_109_out, PB2);
  not not_110 (not_110_out, PB3);
  not not_111 (not_111_out, A);
  not not_112 (not_112_out, PB2);
  not not_113 (not_113_out, SMM);
  not not_114 (not_114_out, A);
  not not_115 (not_115_out, PB2);
  not not_116 (not_116_out, C);
  not not_117 (not_117_out, PB2);
  not not_118 (not_118_out, C);
  not not_119 (not_119_out, PB2);
  not not_120 (not_120_out, A);
  not not_121 (not_121_out, C);
  not not_122 (not_122_out, A);
  not not_123 (not_123_out, C);
  not not_124 (not_124_out, A);
  not not_125 (not_125_out, SMP);
  not not_126 (not_126_out, A);
  not not_127 (not_127_out, SMM);
  not not_128 (not_128_out, A);
  not not_129 (not_129_out, A);
  not not_130 (not_130_out, C);
  not not_131 (not_131_out, SMP);
  not not_132 (not_132_out, SMM);
  not not_133 (not_133_out, SBT);
  not not_134 (not_134_out, C);
  not not_135 (not_135_out, SBT);
  not not_136 (not_136_out, C);
  not not_137 (not_137_out, C);
  not not_138 (not_138_out, C);
  not not_139 (not_139_out, A);
  not not_140 (not_140_out, PB1);
  not not_141 (not_141_out, PB3);
  not not_142 (not_142_out, B);
  not not_143 (not_143_out, PB1);
  not not_144 (not_144_out, PB3);
  not not_145 (not_145_out, A);
  not not_146 (not_146_out, A);
  not not_147 (not_147_out, A);
  not not_148 (not_148_out, B);
  not not_149 (not_149_out, PB2);
  not not_150 (not_150_out, B);
  not not_151 (not_151_out, SMP);
  not not_152 (not_152_out, B);
  not not_153 (not_153_out, SMM);
  not not_154 (not_154_out, B);
  not not_155 (not_155_out, SBT);
  not not_156 (not_156_out, B);
  not not_157 (not_157_out, B);
  not not_158 (not_158_out, A);
  not not_159 (not_159_out, B);
  not not_160 (not_160_out, PB2);
  not not_161 (not_161_out, PB3);
  not not_162 (not_162_out, SBT);
  not not_163 (not_163_out, A);
  not not_164 (not_164_out, B);
  not not_165 (not_165_out, PB2);
  not not_166 (not_166_out, PB3);
  not not_167 (not_167_out, B);
  not not_168 (not_168_out, PB2);
  not not_169 (not_169_out, PB3);
  not not_170 (not_170_out, SMM);
  not not_171 (not_171_out, B);
  not not_172 (not_172_out, PB2);
  not not_173 (not_173_out, PB3);
  not not_174 (not_174_out, A);
  not not_175 (not_175_out, C);
  not not_176 (not_176_out, PB1);
  not not_177 (not_177_out, PB3);
  not not_178 (not_178_out, SMP);
  not not_179 (not_179_out, A);
  not not_180 (not_180_out, C);
  not not_181 (not_181_out, PB1);
  not not_182 (not_182_out, PB3);
  not not_183 (not_183_out, SMM);
  not not_184 (not_184_out, A);
  not not_185 (not_185_out, C);
  not not_186 (not_186_out, PB1);
  not not_187 (not_187_out, PB3);
  not not_188 (not_188_out, C);
  not not_189 (not_189_out, PB1);
  not not_190 (not_190_out, PB3);
  not not_191 (not_191_out, A);
  not not_192 (not_192_out, C);
  not not_193 (not_193_out, PB2);
  not not_194 (not_194_out, PB3);
  not not_195 (not_195_out, B);
  not not_196 (not_196_out, SMP);
  not not_197 (not_197_out, B);
  not not_198 (not_198_out, SMM);
  not not_199 (not_199_out, B);
  not not_200 (not_200_out, B);
  not not_201 (not_201_out, C);
  not not_202 (not_202_out, SBT);
  not not_203 (not_203_out, C);
  not not_204 (not_204_out, C);
  not not_205 (not_205_out, C);
  not not_206 (not_206_out, A);
  not not_207 (not_207_out, B);
  not not_208 (not_208_out, PB1);
  not not_209 (not_209_out, PB2);
  not not_210 (not_210_out, STP);
  not not_211 (not_211_out, A);
  not not_212 (not_212_out, B);
  not not_213 (not_213_out, C);
  not not_214 (not_214_out, PB1);
  not not_215 (not_215_out, PB3);
  not not_216 (not_216_out, SMP);
  not not_217 (not_217_out, A);
  not not_218 (not_218_out, B);
  not not_219 (not_219_out, C);
  not not_220 (not_220_out, PB1);
  not not_221 (not_221_out, PB3);
  not not_222 (not_222_out, SMM);
  not not_223 (not_223_out, B);
  not not_224 (not_224_out, C);
  not not_225 (not_225_out, PB1);
  not not_226 (not_226_out, PB3);
  not not_227 (not_227_out, A);
  not not_228 (not_228_out, B);
  not not_229 (not_229_out, C);
  not not_230 (not_230_out, PB1);
  not not_231 (not_231_out, PB3);
  not not_232 (not_232_out, A);
  not not_233 (not_233_out, PB1);
  not not_234 (not_234_out, PB2);
  not not_235 (not_235_out, A);
  not not_236 (not_236_out, PB1);
  not not_237 (not_237_out, PB2);
  not not_238 (not_238_out, SMP);
  not not_239 (not_239_out, A);
  not not_240 (not_240_out, B);
  not not_241 (not_241_out, PB1);
  not not_242 (not_242_out, PB2);
  not not_243 (not_243_out, A);
  not not_244 (not_244_out, SMP);
  not not_245 (not_245_out, A);
  not not_246 (not_246_out, SMM);
  not not_247 (not_247_out, A);
  not not_248 (not_248_out, A);
  not not_249 (not_249_out, B);
  not not_250 (not_250_out, C);
  not not_251 (not_251_out, STP);
  not not_252 (not_252_out, B);
  not not_253 (not_253_out, C);
  not not_254 (not_254_out, B);
  not not_255 (not_255_out, C);
  not not_256 (not_256_out, B);
  not not_257 (not_257_out, C);
  and and_1 (and_1_out, not_1_out, not_2_out, not_3_out, not_4_out, PB3, not_5_out);
  and and_2 (and_2_out, not_6_out, not_7_out, not_8_out, PB3, SBT);
  and and_3 (and_3_out, not_9_out, not_10_out, not_11_out, not_12_out, PB3, SMM);
  and and_4 (and_4_out, not_13_out, not_14_out, not_15_out, PB3, SMP, not_16_out);
  and and_5 (and_5_out, not_17_out, not_18_out, C, PB1, not_19_out, not_20_out, not_21_out);
  and and_6 (and_6_out, not_22_out, C, PB1, not_23_out, not_24_out, not_25_out, SMM);
  and and_7 (and_7_out, not_26_out, C, PB1, not_27_out, not_28_out, SMP, SBT);
  and and_8 (and_8_out, not_29_out, C, PB1, not_30_out, not_31_out, STP);
  and and_9 (and_9_out, not_32_out, B, not_33_out, not_34_out, PB2, not_35_out, not_36_out);
  and and_10 (and_10_out, not_37_out, B, not_38_out, not_39_out, PB2, not_40_out, not_41_out);
  and and_11 (and_11_out, not_42_out, B, not_43_out, not_44_out, PB2, not_45_out, SBT);
  and and_12 (and_12_out, B, not_46_out, not_47_out, PB2, not_48_out, STP);
  and and_13 (and_13_out, not_49_out, B, not_50_out, PB1, not_51_out, not_52_out);
  and and_14 (and_14_out, A, not_53_out, not_54_out, not_55_out);
  and and_15 (and_15_out, A, not_56_out, not_57_out, SBT);
  and and_16 (and_16_out, A, not_58_out, SMM);
  and and_17 (and_17_out, A, not_59_out, SMP);
  and and_18 (and_18_out, A, not_60_out, STP, SBT);
  and and_19 (and_19_out, A, not_61_out, STP, SMP);
  and and_20 (and_20_out, A, not_62_out, PB3, SBT);
  and and_21 (and_21_out, A, not_63_out, C, not_64_out);
  and and_22 (and_22_out, A, B, not_65_out, not_66_out);
  and and_23 (and_23_out, not_67_out, not_68_out, not_69_out, PB3, STP, not_70_out, not_71_out, not_72_out);
  and and_24 (and_24_out, not_73_out, not_74_out, not_75_out, not_76_out, PB2, not_77_out, not_78_out);
  and and_25 (and_25_out, not_79_out, not_80_out, not_81_out, not_82_out, PB2, not_83_out, not_84_out);
  and and_26 (and_26_out, not_85_out, not_86_out, not_87_out, not_88_out, PB2, not_89_out, SBT);
  and and_27 (and_27_out, not_90_out, not_91_out, not_92_out, not_93_out, PB2, not_94_out, STP);
  and and_28 (and_28_out, not_95_out, not_96_out, C, PB1, not_97_out, not_98_out, not_99_out);
  and and_29 (and_29_out, not_100_out, not_101_out, C, PB1, not_102_out, not_103_out, SMM);
  and and_30 (and_30_out, not_104_out, C, PB1, not_105_out, not_106_out, SMP, not_107_out);
  and and_31 (and_31_out, not_108_out, C, PB1, not_109_out, not_110_out, STP);
  and and_32 (and_32_out, not_111_out, B, not_112_out, not_113_out);
  and and_33 (and_33_out, not_114_out, B, not_115_out, SBT);
  and and_34 (and_34_out, B, not_116_out, not_117_out, SMP);
  and and_35 (and_35_out, B, not_118_out, not_119_out, STP);
  and and_36 (and_36_out, not_120_out, B, not_121_out, PB3);
  and and_37 (and_37_out, not_122_out, B, not_123_out, PB1);
  and and_38 (and_38_out, not_124_out, B, C, not_125_out);
  and and_39 (and_39_out, not_126_out, B, C, not_127_out);
  and and_40 (and_40_out, not_128_out, B, C, SBT);
  and and_41 (and_41_out, not_129_out, B, C, STP);
  and and_42 (and_42_out, A, not_130_out, STP, not_131_out, not_132_out, not_133_out);
  and and_43 (and_43_out, A, B, not_134_out, not_135_out);
  and and_44 (and_44_out, A, B, not_136_out, SMM);
  and and_45 (and_45_out, A, B, not_137_out, SMP);
  and and_46 (and_46_out, A, B, not_138_out, STP);
  and and_47 (and_47_out, not_139_out, not_140_out, PB2, not_141_out);
  and and_48 (and_48_out, not_142_out, C, not_143_out, not_144_out);
  and and_49 (and_49_out, not_145_out, C, PB2);
  and and_50 (and_50_out, not_146_out, C, PB1, PB3);
  and and_51 (and_51_out, not_147_out, B, C);
  and and_52 (and_52_out, A, not_148_out, C, not_149_out);
  and and_53 (and_53_out, A, not_150_out, C, not_151_out);
  and and_54 (and_54_out, A, not_152_out, C, not_153_out);
  and and_55 (and_55_out, A, not_154_out, C, not_155_out);
  and and_56 (and_56_out, A, not_156_out, C, STP);
  and and_57 (and_57_out, A, not_157_out, C, PB3);
  and and_58 (and_58_out, not_158_out, not_159_out, C, PB1, not_160_out, not_161_out, not_162_out);
  and and_59 (and_59_out, not_163_out, not_164_out, C, PB1, not_165_out, not_166_out, SMM);
  and and_60 (and_60_out, not_167_out, C, PB1, not_168_out, not_169_out, SMP, not_170_out);
  and and_61 (and_61_out, not_171_out, C, PB1, not_172_out, not_173_out, STP);
  and and_62 (and_62_out, not_174_out, B, not_175_out, not_176_out, PB2, not_177_out, not_178_out);
  and and_63 (and_63_out, not_179_out, B, not_180_out, not_181_out, PB2, not_182_out, not_183_out);
  and and_64 (and_64_out, not_184_out, B, not_185_out, not_186_out, PB2, not_187_out, SBT);
  and and_65 (and_65_out, B, not_188_out, not_189_out, PB2, not_190_out, STP);
  and and_66 (and_66_out, not_191_out, B, not_192_out, PB1, not_193_out, not_194_out);
  and and_67 (and_67_out, A, not_195_out, C, not_196_out);
  and and_68 (and_68_out, A, not_197_out, C, not_198_out);
  and and_69 (and_69_out, A, not_199_out, C, SBT);
  and and_70 (and_70_out, A, not_200_out, C, STP);
  and and_71 (and_71_out, A, B, not_201_out, not_202_out);
  and and_72 (and_72_out, A, B, not_203_out, SMM);
  and and_73 (and_73_out, A, B, not_204_out, SMP);
  and and_74 (and_74_out, A, B, not_205_out, STP);
  and and_75 (and_75_out, not_206_out, not_207_out, not_208_out, not_209_out, PB3, not_210_out);
  and and_76 (and_76_out, not_211_out, not_212_out, not_213_out, not_214_out, PB2, not_215_out, not_216_out);
  and and_77 (and_77_out, not_217_out, not_218_out, not_219_out, not_220_out, PB2, not_221_out, not_222_out);
  and and_78 (and_78_out, not_223_out, not_224_out, not_225_out, PB2, not_226_out, SBT);
  and and_79 (and_79_out, not_227_out, not_228_out, not_229_out, not_230_out, PB2, not_231_out, STP);
  and and_80 (and_80_out, not_232_out, C, not_233_out, not_234_out, PB3, SBT);
  and and_81 (and_81_out, not_235_out, C, not_236_out, not_237_out, PB3, not_238_out, SMM);
  and and_82 (and_82_out, not_239_out, not_240_out, C, not_241_out, not_242_out, PB3, SMP);
  and and_83 (and_83_out, not_243_out, B, C, not_244_out);
  and and_84 (and_84_out, not_245_out, B, C, not_246_out);
  and and_85 (and_85_out, not_247_out, B, C, SBT);
  and and_86 (and_86_out, not_248_out, B, C, STP);
  and and_87 (and_87_out, A, not_249_out, not_250_out, not_251_out);
  and and_88 (and_88_out, A, not_252_out, not_253_out, SBT);
  and and_89 (and_89_out, A, not_254_out, not_255_out, SMM);
  and and_90 (and_90_out, A, not_256_out, not_257_out, SMP);
  or or_1 (C2, and_47_out, and_48_out, and_49_out, and_50_out, and_51_out, and_52_out, and_53_out, and_54_out, and_55_out, and_56_out, and_57_out);
  or or_2 (A2, and_1_out, and_2_out, and_3_out, and_4_out, and_5_out, and_6_out, and_7_out, and_8_out, and_9_out, and_10_out, and_11_out, and_12_out, and_13_out, and_14_out, and_15_out, and_16_out, and_17_out, and_18_out, and_19_out, and_20_out, and_21_out, and_22_out);
  or or_3 (M0, and_58_out, and_59_out, and_60_out, and_61_out, and_62_out, and_63_out, and_64_out, and_65_out, and_66_out, and_67_out, and_68_out, and_69_out, and_70_out, and_71_out, and_72_out, and_73_out, and_74_out);
  or or_4 (M1, and_75_out, and_76_out, and_77_out, and_78_out, and_79_out, and_80_out, and_81_out, and_82_out, and_83_out, and_84_out, and_85_out, and_86_out, and_87_out, and_88_out, and_89_out, and_90_out);
  or or_5 (B2, and_23_out, and_24_out, and_25_out, and_26_out, and_27_out, and_28_out, and_29_out, and_30_out, and_31_out, and_32_out, and_33_out, and_34_out, and_35_out, and_36_out, and_37_out, and_38_out, and_39_out, and_40_out, and_41_out, and_42_out, and_43_out, and_44_out, and_45_out, and_46_out);
endmodule

module Lift2 (
  input  A,
  input  B,
  input  C,
  input  PB1,
  input  PB2,
  input  PB3,
  input  STP,
  input  SMP,
  input  SMM,
  input  SBT,
  output A2,
  output B2,
  output C2,
  output M0,
  output M1
);

  wire and_1_out, and_2_out, and_3_out, and_4_out, and_5_out, and_6_out, and_7_out, and_8_out, and_9_out,
       and_10_out, and_11_out, and_12_out, and_13_out, and_14_out, and_15_out, and_16_out, and_17_out,
       and_18_out, and_19_out, and_20_out, and_21_out, and_22_out, and_23_out, and_24_out, and_25_out,
       and_26_out, and_27_out, and_28_out, and_29_out, and_30_out, and_31_out, and_32_out, and_33_out,
       and_34_out, and_35_out, and_36_out, and_37_out, and_38_out, and_39_out, and_40_out, and_41_out,
       and_42_out, and_43_out, and_44_out, and_45_out, and_46_out, and_47_out, and_48_out, and_49_out,
       and_50_out, and_51_out, and_52_out, and_53_out, and_54_out, and_55_out, and_56_out, and_57_out,
       and_58_out, and_59_out, and_60_out, and_61_out, and_62_out, and_63_out, and_64_out, and_65_out,
       not_1_out, not_2_out, not_3_out, not_4_out, not_5_out, not_6_out, not_7_out, not_8_out, not_9_out,
       not_10_out, not_11_out, not_12_out, not_13_out, not_14_out, not_15_out, not_16_out, not_17_out,
       not_18_out, not_19_out, not_20_out, not_21_out, not_22_out, not_23_out, not_24_out, not_25_out,
       not_26_out, not_27_out, not_28_out, not_29_out, not_30_out, not_31_out, not_32_out, not_33_out,
       not_34_out, not_35_out, not_36_out, not_37_out, not_38_out, not_39_out, not_40_out, not_41_out,
       not_42_out, not_43_out, not_44_out, not_45_out, not_46_out, not_47_out, not_48_out, not_49_out,
       not_50_out, not_51_out, not_52_out, not_53_out, not_54_out, not_55_out, not_56_out, not_57_out,
       not_58_out, not_59_out, not_60_out, not_61_out, not_62_out, not_63_out, not_64_out, not_65_out,
       not_66_out, not_67_out, not_68_out, not_69_out, not_70_out, not_71_out, not_72_out, not_73_out,
       not_74_out, not_75_out, not_76_out, not_77_out, not_78_out, not_79_out, not_80_out, not_81_out,
       not_82_out, not_83_out, not_84_out, not_85_out, not_86_out, not_87_out, not_88_out, not_89_out,
       not_90_out, not_91_out, not_92_out, not_93_out, not_94_out, not_95_out, not_96_out, not_97_out,
       not_98_out, not_99_out, not_100_out, not_101_out, not_102_out, not_103_out, not_104_out, not_105_out,
       not_106_out, not_107_out, not_108_out, not_109_out, not_110_out, not_111_out, not_112_out,
       not_113_out, not_114_out, not_115_out, not_116_out, not_117_out, not_118_out, not_119_out,
       not_120_out, not_121_out, not_122_out, not_123_out, not_124_out, not_125_out, not_126_out,
       not_127_out, not_128_out, not_129_out, not_130_out, not_131_out, not_132_out, not_133_out,
       not_134_out, not_135_out, not_136_out, not_137_out, not_138_out, not_139_out, not_140_out,
       not_141_out, not_142_out, not_143_out, not_144_out, not_145_out, not_146_out, not_147_out,
       not_148_out, not_149_out, not_150_out, not_151_out, not_152_out, not_153_out, not_154_out,
       not_155_out, not_156_out, not_157_out, not_158_out, not_159_out, not_160_out, not_161_out,
       not_162_out, not_163_out, not_164_out, not_165_out, not_166_out, not_167_out, not_168_out,
       not_169_out, not_170_out, not_171_out, not_172_out, not_173_out, not_174_out, not_175_out,
       not_176_out, not_177_out, not_178_out, not_179_out, not_180_out, not_181_out, not_182_out,
       not_183_out, not_184_out, not_185_out, not_186_out, not_187_out, not_188_out, not_189_out,
       not_190_out, not_191_out, not_192_out, not_193_out, not_194_out, not_195_out, not_196_out,
       not_197_out, not_198_out, not_199_out, not_200_out, not_201_out, not_202_out, not_203_out,
       not_204_out, not_205_out, not_206_out, not_207_out, not_208_out, not_209_out, not_210_out,
       not_211_out, not_212_out, not_213_out, not_214_out, not_215_out, not_216_out, not_217_out,
       not_218_out, not_219_out, not_220_out, not_221_out, not_222_out, not_223_out, not_224_out,
       not_225_out, not_226_out, not_227_out, not_228_out, not_229_out, not_230_out, not_231_out,
       not_232_out, not_233_out, not_234_out;

  not not_1 (not_1_out, B);
  not not_2 (not_2_out, PB1);
  not not_3 (not_3_out, PB2);
  not not_4 (not_4_out, STP);
  not not_5 (not_5_out, SMP);
  not not_6 (not_6_out, A);
  not not_7 (not_7_out, B);
  not not_8 (not_8_out, PB1);
  not not_9 (not_9_out, PB2);
  not not_10 (not_10_out, A);
  not not_11 (not_11_out, B);
  not not_12 (not_12_out, PB1);
  not not_13 (not_13_out, PB2);
  not not_14 (not_14_out, A);
  not not_15 (not_15_out, B);
  not not_16 (not_16_out, PB1);
  not not_17 (not_17_out, PB2);
  not not_18 (not_18_out, A);
  not not_19 (not_19_out, B);
  not not_20 (not_20_out, PB2);
  not not_21 (not_21_out, PB3);
  not not_22 (not_22_out, SBT);
  not not_23 (not_23_out, B);
  not not_24 (not_24_out, PB2);
  not not_25 (not_25_out, PB3);
  not not_26 (not_26_out, SMP);
  not not_27 (not_27_out, A);
  not not_28 (not_28_out, B);
  not not_29 (not_29_out, PB2);
  not not_30 (not_30_out, PB3);
  not not_31 (not_31_out, A);
  not not_32 (not_32_out, B);
  not not_33 (not_33_out, PB2);
  not not_34 (not_34_out, PB3);
  not not_35 (not_35_out, C);
  not not_36 (not_36_out, PB1);
  not not_37 (not_37_out, PB3);
  not not_38 (not_38_out, SMP);
  not not_39 (not_39_out, SBT);
  not not_40 (not_40_out, C);
  not not_41 (not_41_out, PB1);
  not not_42 (not_42_out, PB3);
  not not_43 (not_43_out, SMM);
  not not_44 (not_44_out, SBT);
  not not_45 (not_45_out, A);
  not not_46 (not_46_out, C);
  not not_47 (not_47_out, PB1);
  not not_48 (not_48_out, PB3);
  not not_49 (not_49_out, C);
  not not_50 (not_50_out, PB1);
  not not_51 (not_51_out, PB3);
  not not_52 (not_52_out, SBT);
  not not_53 (not_53_out, A);
  not not_54 (not_54_out, C);
  not not_55 (not_55_out, PB2);
  not not_56 (not_56_out, PB3);
  not not_57 (not_57_out, B);
  not not_58 (not_58_out, C);
  not not_59 (not_59_out, STP);
  not not_60 (not_60_out, B);
  not not_61 (not_61_out, SMP);
  not not_62 (not_62_out, B);
  not not_63 (not_63_out, SMM);
  not not_64 (not_64_out, C);
  not not_65 (not_65_out, SBT);
  not not_66 (not_66_out, A);
  not not_67 (not_67_out, PB1);
  not not_68 (not_68_out, PB2);
  not not_69 (not_69_out, SMP);
  not not_70 (not_70_out, SMM);
  not not_71 (not_71_out, SBT);
  not not_72 (not_72_out, A);
  not not_73 (not_73_out, B);
  not not_74 (not_74_out, C);
  not not_75 (not_75_out, PB1);
  not not_76 (not_76_out, PB3);
  not not_77 (not_77_out, SMP);
  not not_78 (not_78_out, A);
  not not_79 (not_79_out, B);
  not not_80 (not_80_out, C);
  not not_81 (not_81_out, PB1);
  not not_82 (not_82_out, PB3);
  not not_83 (not_83_out, SMM);
  not not_84 (not_84_out, A);
  not not_85 (not_85_out, B);
  not not_86 (not_86_out, C);
  not not_87 (not_87_out, PB1);
  not not_88 (not_88_out, PB3);
  not not_89 (not_89_out, B);
  not not_90 (not_90_out, C);
  not not_91 (not_91_out, PB1);
  not not_92 (not_92_out, PB3);
  not not_93 (not_93_out, A);
  not not_94 (not_94_out, B);
  not not_95 (not_95_out, PB2);
  not not_96 (not_96_out, PB3);
  not not_97 (not_97_out, SBT);
  not not_98 (not_98_out, A);
  not not_99 (not_99_out, B);
  not not_100 (not_100_out, PB2);
  not not_101 (not_101_out, PB3);
  not not_102 (not_102_out, A);
  not not_103 (not_103_out, PB2);
  not not_104 (not_104_out, PB3);
  not not_105 (not_105_out, SMM);
  not not_106 (not_106_out, A);
  not not_107 (not_107_out, PB2);
  not not_108 (not_108_out, PB3);
  not not_109 (not_109_out, SMP);
  not not_110 (not_110_out, A);
  not not_111 (not_111_out, PB2);
  not not_112 (not_112_out, SMM);
  not not_113 (not_113_out, A);
  not not_114 (not_114_out, PB2);
  not not_115 (not_115_out, SMP);
  not not_116 (not_116_out, A);
  not not_117 (not_117_out, C);
  not not_118 (not_118_out, PB2);
  not not_119 (not_119_out, A);
  not not_120 (not_120_out, PB2);
  not not_121 (not_121_out, SMP);
  not not_122 (not_122_out, A);
  not not_123 (not_123_out, C);
  not not_124 (not_124_out, A);
  not not_125 (not_125_out, C);
  not not_126 (not_126_out, A);
  not not_127 (not_127_out, SMP);
  not not_128 (not_128_out, A);
  not not_129 (not_129_out, SMM);
  not not_130 (not_130_out, B);
  not not_131 (not_131_out, C);
  not not_132 (not_132_out, C);
  not not_133 (not_133_out, SBT);
  not not_134 (not_134_out, A);
  not not_135 (not_135_out, PB1);
  not not_136 (not_136_out, PB3);
  not not_137 (not_137_out, B);
  not not_138 (not_138_out, PB1);
  not not_139 (not_139_out, PB3);
  not not_140 (not_140_out, A);
  not not_141 (not_141_out, A);
  not not_142 (not_142_out, A);
  not not_143 (not_143_out, B);
  not not_144 (not_144_out, A);
  not not_145 (not_145_out, B);
  not not_146 (not_146_out, PB2);
  not not_147 (not_147_out, PB3);
  not not_148 (not_148_out, SBT);
  not not_149 (not_149_out, B);
  not not_150 (not_150_out, PB2);
  not not_151 (not_151_out, PB3);
  not not_152 (not_152_out, SMP);
  not not_153 (not_153_out, A);
  not not_154 (not_154_out, B);
  not not_155 (not_155_out, PB2);
  not not_156 (not_156_out, PB3);
  not not_157 (not_157_out, B);
  not not_158 (not_158_out, PB2);
  not not_159 (not_159_out, PB3);
  not not_160 (not_160_out, SMP);
  not not_161 (not_161_out, C);
  not not_162 (not_162_out, PB1);
  not not_163 (not_163_out, PB3);
  not not_164 (not_164_out, SMP);
  not not_165 (not_165_out, SBT);
  not not_166 (not_166_out, C);
  not not_167 (not_167_out, PB1);
  not not_168 (not_168_out, PB3);
  not not_169 (not_169_out, SMM);
  not not_170 (not_170_out, SBT);
  not not_171 (not_171_out, A);
  not not_172 (not_172_out, C);
  not not_173 (not_173_out, PB1);
  not not_174 (not_174_out, PB3);
  not not_175 (not_175_out, C);
  not not_176 (not_176_out, PB1);
  not not_177 (not_177_out, PB3);
  not not_178 (not_178_out, SBT);
  not not_179 (not_179_out, A);
  not not_180 (not_180_out, C);
  not not_181 (not_181_out, PB2);
  not not_182 (not_182_out, PB3);
  not not_183 (not_183_out, B);
  not not_184 (not_184_out, SMP);
  not not_185 (not_185_out, B);
  not not_186 (not_186_out, SMM);
  not not_187 (not_187_out, C);
  not not_188 (not_188_out, SBT);
  not not_189 (not_189_out, A);
  not not_190 (not_190_out, B);
  not not_191 (not_191_out, PB1);
  not not_192 (not_192_out, PB2);
  not not_193 (not_193_out, STP);
  not not_194 (not_194_out, B);
  not not_195 (not_195_out, C);
  not not_196 (not_196_out, PB1);
  not not_197 (not_197_out, PB3);
  not not_198 (not_198_out, STP);
  not not_199 (not_199_out, SMP);
  not not_200 (not_200_out, B);
  not not_201 (not_201_out, C);
  not not_202 (not_202_out, PB1);
  not not_203 (not_203_out, PB3);
  not not_204 (not_204_out, STP);
  not not_205 (not_205_out, SMM);
  not not_206 (not_206_out, B);
  not not_207 (not_207_out, C);
  not not_208 (not_208_out, PB1);
  not not_209 (not_209_out, PB3);
  not not_210 (not_210_out, STP);
  not not_211 (not_211_out, A);
  not not_212 (not_212_out, B);
  not not_213 (not_213_out, C);
  not not_214 (not_214_out, PB1);
  not not_215 (not_215_out, PB3);
  not not_216 (not_216_out, A);
  not not_217 (not_217_out, PB1);
  not not_218 (not_218_out, PB2);
  not not_219 (not_219_out, SMP);
  not not_220 (not_220_out, A);
  not not_221 (not_221_out, PB1);
  not not_222 (not_222_out, PB2);
  not not_223 (not_223_out, SMP);
  not not_224 (not_224_out, A);
  not not_225 (not_225_out, B);
  not not_226 (not_226_out, PB1);
  not not_227 (not_227_out, PB2);
  not not_228 (not_228_out, A);
  not not_229 (not_229_out, SMP);
  not not_230 (not_230_out, A);
  not not_231 (not_231_out, SMM);
  not not_232 (not_232_out, B);
  not not_233 (not_233_out, C);
  not not_234 (not_234_out, STP);
  and and_1 (and_1_out, not_1_out, not_2_out, not_3_out, PB3, not_4_out, not_5_out);
  and and_2 (and_2_out, not_6_out, not_7_out, not_8_out, not_9_out, PB3, SBT);
  and and_3 (and_3_out, not_10_out, not_11_out, not_12_out, not_13_out, PB3, SMM);
  and and_4 (and_4_out, not_14_out, not_15_out, not_16_out, not_17_out, PB3, SMP);
  and and_5 (and_5_out, not_18_out, not_19_out, C, PB1, not_20_out, not_21_out, not_22_out);
  and and_6 (and_6_out, not_23_out, C, PB1, not_24_out, not_25_out, not_26_out, SMM);
  and and_7 (and_7_out, not_27_out, not_28_out, C, PB1, not_29_out, not_30_out, SMP);
  and and_8 (and_8_out, not_31_out, not_32_out, C, PB1, not_33_out, not_34_out, STP);
  and and_9 (and_9_out, B, not_35_out, not_36_out, PB2, not_37_out, not_38_out, not_39_out);
  and and_10 (and_10_out, B, not_40_out, not_41_out, PB2, not_42_out, not_43_out, not_44_out);
  and and_11 (and_11_out, not_45_out, B, not_46_out, not_47_out, PB2, not_48_out, SBT);
  and and_12 (and_12_out, B, not_49_out, not_50_out, PB2, not_51_out, STP, not_52_out);
  and and_13 (and_13_out, not_53_out, B, not_54_out, PB1, not_55_out, not_56_out);
  and and_14 (and_14_out, A, not_57_out, not_58_out, not_59_out);
  and and_15 (and_15_out, A, not_60_out, C, not_61_out);
  and and_16 (and_16_out, A, not_62_out, C, not_63_out);
  and and_17 (and_17_out, A, B, not_64_out, not_65_out);
  and and_18 (and_18_out, not_66_out, not_67_out, not_68_out, PB3, STP, not_69_out, not_70_out, not_71_out);
  and and_19 (and_19_out, not_72_out, not_73_out, not_74_out, not_75_out, PB2, not_76_out, not_77_out);
  and and_20 (and_20_out, not_78_out, not_79_out, not_80_out, not_81_out, PB2, not_82_out, not_83_out);
  and and_21 (and_21_out, not_84_out, not_85_out, not_86_out, not_87_out, PB2, not_88_out, SBT);
  and and_22 (and_22_out, not_89_out, not_90_out, not_91_out, PB2, not_92_out, STP);
  and and_23 (and_23_out, not_93_out, not_94_out, C, PB1, not_95_out, not_96_out, not_97_out);
  and and_24 (and_24_out, not_98_out, not_99_out, C, PB1, not_100_out, not_101_out, SMM);
  and and_25 (and_25_out, not_102_out, C, PB1, not_103_out, not_104_out, SMP, not_105_out);
  and and_26 (and_26_out, not_106_out, C, PB1, not_107_out, not_108_out, STP, not_109_out);
  and and_27 (and_27_out, not_110_out, B, not_111_out, not_112_out);
  and and_28 (and_28_out, not_113_out, B, not_114_out, not_115_out, SBT);
  and and_29 (and_29_out, not_116_out, B, not_117_out, not_118_out, SMP);
  and and_30 (and_30_out, not_119_out, B, not_120_out, STP, not_121_out);
  and and_31 (and_31_out, not_122_out, B, not_123_out, PB3);
  and and_32 (and_32_out, not_124_out, B, not_125_out, PB1);
  and and_33 (and_33_out, not_126_out, B, C, not_127_out);
  and and_34 (and_34_out, not_128_out, B, C, not_129_out);
  and and_35 (and_35_out, A, not_130_out, not_131_out, STP);
  and and_36 (and_36_out, A, B, not_132_out, not_133_out);
  and and_37 (and_37_out, not_134_out, not_135_out, PB2, not_136_out);
  and and_38 (and_38_out, not_137_out, C, not_138_out, not_139_out);
  and and_39 (and_39_out, not_140_out, C, PB2);
  and and_40 (and_40_out, not_141_out, C, PB1, PB3);
  and and_41 (and_41_out, not_142_out, B, C);
  and and_42 (and_42_out, A, not_143_out, C);
  and and_43 (and_43_out, not_144_out, not_145_out, C, PB1, not_146_out, not_147_out, not_148_out);
  and and_44 (and_44_out, not_149_out, C, PB1, not_150_out, not_151_out, not_152_out, SMM);
  and and_45 (and_45_out, not_153_out, not_154_out, C, PB1, not_155_out, not_156_out, SMP);
  and and_46 (and_46_out, not_157_out, C, PB1, not_158_out, not_159_out, STP, not_160_out);
  and and_47 (and_47_out, B, not_161_out, not_162_out, PB2, not_163_out, not_164_out, not_165_out);
  and and_48 (and_48_out, B, not_166_out, not_167_out, PB2, not_168_out, not_169_out, not_170_out);
  and and_49 (and_49_out, not_171_out, B, not_172_out, not_173_out, PB2, not_174_out, SBT);
  and and_50 (and_50_out, B, not_175_out, not_176_out, PB2, not_177_out, STP, not_178_out);
  and and_51 (and_51_out, not_179_out, B, not_180_out, PB1, not_181_out, not_182_out);
  and and_52 (and_52_out, A, not_183_out, C, not_184_out);
  and and_53 (and_53_out, A, not_185_out, C, not_186_out);
  and and_54 (and_54_out, A, B, not_187_out, not_188_out);
  and and_55 (and_55_out, not_189_out, not_190_out, not_191_out, not_192_out, PB3, not_193_out);
  and and_56 (and_56_out, not_194_out, not_195_out, not_196_out, PB2, not_197_out, not_198_out, not_199_out);
  and and_57 (and_57_out, not_200_out, not_201_out, not_202_out, PB2, not_203_out, not_204_out, not_205_out);
  and and_58 (and_58_out, not_206_out, not_207_out, not_208_out, PB2, not_209_out, not_210_out, SBT);
  and and_59 (and_59_out, not_211_out, not_212_out, not_213_out, not_214_out, PB2, not_215_out, STP);
  and and_60 (and_60_out, not_216_out, C, not_217_out, not_218_out, PB3, not_219_out, SBT);
  and and_61 (and_61_out, not_220_out, C, not_221_out, not_222_out, PB3, not_223_out, SMM);
  and and_62 (and_62_out, not_224_out, not_225_out, C, not_226_out, not_227_out, PB3, SMP);
  and and_63 (and_63_out, not_228_out, B, C, not_229_out);
  and and_64 (and_64_out, not_230_out, B, C, not_231_out);
  and and_65 (and_65_out, A, not_232_out, not_233_out, not_234_out);
  or or_1 (C2, and_37_out, and_38_out, and_39_out, and_40_out, and_41_out, and_42_out);
  or or_2 (A2, and_1_out, and_2_out, and_3_out, and_4_out, and_5_out, and_6_out, and_7_out, and_8_out, and_9_out, and_10_out, and_11_out, and_12_out, and_13_out, and_14_out, and_15_out, and_16_out, and_17_out);
  or or_3 (B2, and_18_out, and_19_out, and_20_out, and_21_out, and_22_out, and_23_out, and_24_out, and_25_out, and_26_out, and_27_out, and_28_out, and_29_out, and_30_out, and_31_out, and_32_out, and_33_out, and_34_out, and_35_out, and_36_out);
  or or_4 (M0, and_43_out, and_44_out, and_45_out, and_46_out, and_47_out, and_48_out, and_49_out, and_50_out, and_51_out, and_52_out, and_53_out, and_54_out);
  or or_5 (M1, and_55_out, and_56_out, and_57_out, and_58_out, and_59_out, and_60_out, and_61_out, and_62_out, and_63_out, and_64_out, and_65_out);
endmodule

module Lift3 (
  input  A,
  input  B,
  input  C,
  input  PB1,
  input  PB2,
  input  PB3,
  input  STP,
  input  SMP,
  input  SMM,
  input  SBT,
  output A2,
  output B2,
  output C2,
  output M0,
  output M1
);

  wire and_1_out, and_2_out, and_3_out, and_4_out, and_5_out, and_6_out, and_8_out, and_9_out, and_10_out,
       and_11_out, and_12_out, and_13_out, and_14_out, and_15_out, and_16_out, and_17_out, and_18_out,
       and_19_out, and_20_out, and_21_out, and_22_out, and_23_out, and_24_out, and_25_out, and_26_out,
       and_27_out, and_28_out, and_29_out, and_30_out, and_31_out, and_32_out, and_33_out, and_34_out,
       and_35_out, and_36_out, and_37_out, and_38_out, and_39_out, and_40_out, and_41_out, nand_1_out,
       nand_2_out, not_1_out, not_2_out, not_3_out, not_4_out, not_5_out, not_6_out, not_7_out, not_8_out,
       not_9_out, not_10_out, not_11_out, not_12_out, not_13_out, not_14_out, not_15_out, not_16_out,
       not_17_out, not_18_out, not_19_out, not_20_out, not_21_out, not_22_out, not_23_out, not_24_out,
       not_25_out, not_26_out, not_27_out, not_28_out, not_29_out, not_30_out, not_31_out, not_32_out,
       not_33_out, not_34_out, not_35_out, not_36_out, not_37_out, not_38_out, not_39_out, not_40_out,
       not_41_out, not_42_out, not_43_out, not_44_out, not_45_out, not_46_out, not_47_out, not_48_out,
       not_49_out, not_50_out, not_51_out, not_52_out, not_53_out, not_54_out, not_55_out, not_56_out,
       not_57_out, not_58_out, not_59_out, not_60_out, not_61_out, not_62_out, not_63_out, not_64_out,
       not_65_out, not_66_out, not_67_out, not_68_out, not_69_out, not_70_out, not_71_out, not_72_out,
       not_73_out, not_74_out, not_75_out, not_76_out, not_77_out, not_78_out, not_79_out, not_80_out,
       not_81_out, not_82_out, or_1_out, or_2_out, or_3_out, or_4_out, or_5_out, or_8_out, or_9_out,
       or_10_out, or_11_out, or_12_out, or_13_out, or_14_out, xor_1_out;

  not not_1 (not_1_out, SBT);
  nand nand_1 (nand_1_out, SMP, SMM);
  not not_2 (not_2_out, SMP);
  not not_3 (not_3_out, SMM);
  not not_4 (not_4_out, SBT);
  not not_5 (not_5_out, A);
  not not_6 (not_6_out, PB1);
  not not_7 (not_7_out, PB3);
  not not_8 (not_8_out, B);
  not not_9 (not_9_out, PB1);
  not not_10 (not_10_out, PB3);
  not not_11 (not_11_out, A);
  not not_12 (not_12_out, A);
  not not_13 (not_13_out, A);
  not not_14 (not_14_out, B);
  xor xor_1 (xor_1_out, B, C);
  not not_15 (not_15_out, A);
  not not_16 (not_16_out, B);
  not not_17 (not_17_out, C);
  not not_18 (not_18_out, STP);
  not not_19 (not_19_out, SMP);
  not not_20 (not_20_out, A);
  or or_1 (or_1_out, SBT, SMM, SMP);
  not not_21 (not_21_out, SMP);
  not not_22 (not_22_out, A);
  or or_2 (or_2_out, not_1_out, SMP, STP);
  not not_23 (not_23_out, SBT);
  or or_3 (or_3_out, nand_1_out, STP);
  not not_24 (not_24_out, A);
  not not_25 (not_25_out, C);
  not not_26 (not_26_out, STP);
  nand nand_2 (nand_2_out, SMP, SMM);
  not not_27 (not_27_out, A);
  not not_28 (not_28_out, PB2);
  not not_29 (not_29_out, PB3);
  not not_30 (not_30_out, SBT);
  not not_31 (not_31_out, A);
  or or_4 (or_4_out, not_2_out, not_3_out, SBT);
  not not_32 (not_32_out, B);
  or or_5 (or_5_out, not_4_out, SMM);
  not not_33 (not_33_out, SMM);
  not not_34 (not_34_out, SMP);
  and and_1 (and_1_out, not_5_out, not_6_out, PB2, not_7_out);
  and and_2 (and_2_out, not_8_out, C, not_9_out, not_10_out);
  and and_3 (and_3_out, not_11_out, C, PB2);
  and and_4 (and_4_out, not_12_out, C, PB1, PB3);
  and and_5 (and_5_out, not_13_out, B, C);
  and and_6 (and_6_out, A, not_14_out, C);
  and and_7 (M0, A, xor_1_out);
  and and_8 (and_8_out, not_15_out, B, C);
  and and_9 (and_9_out, A, not_16_out, not_17_out);
  and and_10 (and_10_out, not_18_out, not_19_out);
  and and_11 (and_11_out, not_20_out, or_1_out);
  and and_12 (and_12_out, not_21_out, SMM);
  and and_13 (and_13_out, not_22_out, or_2_out);
  and and_14 (and_14_out, not_23_out, or_3_out);
  and and_15 (and_15_out, not_24_out, SBT);
  and and_16 (and_16_out, not_25_out, not_26_out);
  and and_17 (and_17_out, C, nand_2_out);
  and and_18 (and_18_out, not_27_out, PB1, not_28_out, not_29_out);
  and and_19 (and_19_out, A, not_30_out);
  and and_20 (and_20_out, not_31_out, or_4_out);
  and and_21 (and_21_out, not_32_out, or_5_out);
  and and_22 (and_22_out, SMP, not_33_out);
  and and_23 (and_23_out, STP, not_34_out);
  or or_6 (C2, and_1_out, and_2_out, and_3_out, and_4_out, and_5_out, and_6_out);
  or or_7 (M1, and_8_out, and_9_out);
  not not_35 (not_35_out, B);
  not not_36 (not_36_out, PB1);
  not not_37 (not_37_out, PB2);
  or or_8 (or_8_out, and_10_out, and_11_out);
  not not_38 (not_38_out, B);
  not not_39 (not_39_out, PB2);
  not not_40 (not_40_out, PB3);
  or or_9 (or_9_out, and_12_out, and_13_out);
  not not_41 (not_41_out, C);
  not not_42 (not_42_out, PB1);
  not not_43 (not_43_out, PB3);
  or or_10 (or_10_out, and_14_out, and_15_out);
  not not_44 (not_44_out, B);
  or or_11 (or_11_out, and_16_out, and_17_out);
  not not_45 (not_45_out, C);
  or or_12 (or_12_out, and_18_out, and_19_out);
  not not_46 (not_46_out, A);
  not not_47 (not_47_out, PB1);
  not not_48 (not_48_out, PB2);
  not not_49 (not_49_out, SMP);
  not not_50 (not_50_out, SMM);
  not not_51 (not_51_out, SBT);
  not not_52 (not_52_out, B);
  not not_53 (not_53_out, C);
  not not_54 (not_54_out, PB1);
  not not_55 (not_55_out, PB3);
  or or_13 (or_13_out, and_20_out, STP);
  not not_56 (not_56_out, A);
  not not_57 (not_57_out, PB2);
  not not_58 (not_58_out, PB3);
  or or_14 (or_14_out, and_21_out, and_22_out, and_23_out);
  not not_59 (not_59_out, A);
  not not_60 (not_60_out, PB2);
  not not_61 (not_61_out, SMM);
  not not_62 (not_62_out, A);
  not not_63 (not_63_out, PB2);
  not not_64 (not_64_out, SMP);
  not not_65 (not_65_out, A);
  not not_66 (not_66_out, C);
  not not_67 (not_67_out, PB2);
  not not_68 (not_68_out, A);
  not not_69 (not_69_out, PB2);
  not not_70 (not_70_out, SMP);
  not not_71 (not_71_out, A);
  not not_72 (not_72_out, C);
  not not_73 (not_73_out, A);
  not not_74 (not_74_out, C);
  not not_75 (not_75_out, A);
  not not_76 (not_76_out, SMP);
  not not_77 (not_77_out, A);
  not not_78 (not_78_out, SMM);
  not not_79 (not_79_out, B);
  not not_80 (not_80_out, C);
  not not_81 (not_81_out, C);
  not not_82 (not_82_out, SBT);
  and and_24 (and_24_out, not_35_out, not_36_out, not_37_out, PB3, or_8_out);
  and and_25 (and_25_out, not_38_out, C, PB1, not_39_out, not_40_out, or_9_out);
  and and_26 (and_26_out, B, not_41_out, not_42_out, PB2, not_43_out, or_10_out);
  and and_27 (and_27_out, A, not_44_out, or_11_out);
  and and_28 (and_28_out, B, not_45_out, or_12_out);
  and and_29 (and_29_out, not_46_out, not_47_out, not_48_out, PB3, STP, not_49_out, not_50_out, not_51_out);
  and and_30 (and_30_out, not_52_out, not_53_out, not_54_out, PB2, not_55_out, or_13_out);
  and and_31 (and_31_out, not_56_out, C, PB1, not_57_out, not_58_out, or_14_out);
  and and_32 (and_32_out, not_59_out, B, not_60_out, not_61_out);
  and and_33 (and_33_out, not_62_out, B, not_63_out, not_64_out, SBT);
  and and_34 (and_34_out, not_65_out, B, not_66_out, not_67_out, SMP);
  and and_35 (and_35_out, not_68_out, B, not_69_out, STP, not_70_out);
  and and_36 (and_36_out, not_71_out, B, not_72_out, PB3);
  and and_37 (and_37_out, not_73_out, B, not_74_out, PB1);
  and and_38 (and_38_out, not_75_out, B, C, not_76_out);
  and and_39 (and_39_out, not_77_out, B, C, not_78_out);
  and and_40 (and_40_out, A, not_79_out, not_80_out, STP);
  and and_41 (and_41_out, A, B, not_81_out, not_82_out);
  or or_15 (A2, and_24_out, and_25_out, and_26_out, and_27_out, and_28_out);
  or or_16 (B2, and_29_out, and_30_out, and_31_out, and_32_out, and_33_out, and_34_out, and_35_out, and_36_out, and_37_out, and_38_out, and_39_out, and_40_out, and_41_out);
endmodule
